// Logisim project Project.circ as structural Verilog: 5 circuits, main circuit main
module main (
  input  EN
);

  wire clock_1_out, controlunit_1_en_2, videochip_1_en_2, videochip_2_en_2, videochip_3_en_2;
  wire [1:0] videochip_1_id_2, videochip_2_id_2, videochip_3_id_2;
  wire [3:0] joystick_1_y, joystick_2_y;
  wire [4:0] controlunit_1_ballx, controlunit_1_bally, controlunit_1_leftbaty, controlunit_1_out_11,
       videochip_1_ballx_2, videochip_1_bally_2, videochip_1_leftbaty_2, videochip_1_rightbaty_2,
       videochip_2_ballx_2, videochip_2_bally_2, videochip_2_leftbaty_2, videochip_2_rightbaty_2,
       videochip_3_ballx_2, videochip_3_bally_2, videochip_3_leftbaty_2, videochip_3_rightbaty_2;
  wire [7:0] Enemy_Score, My_Score;
  wire [31:0] videochip_1_out_13, videochip_1_out_14, videochip_1_out_15, videochip_1_out_16,
       videochip_1_out_17, videochip_1_out_18, videochip_1_out_19, videochip_1_out_20, videochip_2_out_13,
       videochip_2_out_14, videochip_2_out_15, videochip_2_out_16, videochip_2_out_17, videochip_2_out_18,
       videochip_2_out_19, videochip_2_out_20, videochip_3_out_13, videochip_3_out_14, videochip_3_out_15,
       videochip_3_out_16, videochip_3_out_17, videochip_3_out_18, videochip_3_out_19, videochip_3_out_20,
       videochip_4_out_13, videochip_4_out_14, videochip_4_out_15, videochip_4_out_16, videochip_4_out_17,
       videochip_4_out_18, videochip_4_out_19, videochip_4_out_20;

  Clock clock_1 (.out(clock_1_out));
  Joystick joystick_1 (.y(joystick_1_y));  // open: x
  Joystick joystick_2 (.y(joystick_2_y));  // open: x
  Hex_Digit_Display hex_digit_display_1 (.value(My_Score[3:0]));  // open: dp
  Hex_Digit_Display hex_digit_display_2 (.value(My_Score[7:4]));  // open: dp
  ControlUnit controlunit_1 (
    .Clock(clock_1_out), .Joystick(joystick_1_y), .BallX(controlunit_1_ballx), .BallY(controlunit_1_bally),
    .LeftBatY(controlunit_1_leftbaty), .EN(EN), .EN_2(controlunit_1_en_2), .RightBatY(joystick_2_y),
    .out_11(controlunit_1_out_11), .Enemy_Score(Enemy_Score), .My_Score(My_Score));
  DotMatrix #(.matrixcols(32), .matrixrows(32)) dotmatrix_1 (
    .col0(videochip_1_out_13), .col1(videochip_1_out_14), .col2(videochip_1_out_15),
    .col3(videochip_1_out_16), .col4(videochip_1_out_17), .col5(videochip_1_out_18),
    .col6(videochip_1_out_19), .col7(videochip_1_out_20), .col8(videochip_2_out_13),
    .col9(videochip_2_out_14), .col10(videochip_2_out_15), .col11(videochip_2_out_16),
    .col12(videochip_2_out_17), .col13(videochip_2_out_18), .col14(videochip_2_out_19),
    .col15(videochip_2_out_20), .col16(videochip_3_out_13), .col17(videochip_3_out_14),
    .col18(videochip_3_out_15), .col19(videochip_3_out_16), .col20(videochip_3_out_17),
    .col21(videochip_3_out_18), .col22(videochip_3_out_19), .col23(videochip_3_out_20),
    .col24(videochip_4_out_13), .col25(videochip_4_out_14), .col26(videochip_4_out_15),
    .col27(videochip_4_out_16), .col28(videochip_4_out_17), .col29(videochip_4_out_18),
    .col30(videochip_4_out_19), .col31(videochip_4_out_20));
  VideoChip videochip_1 (
    .ballY(controlunit_1_bally), .out_13(videochip_1_out_13), .out_14(videochip_1_out_14),
    .out_15(videochip_1_out_15), .out_16(videochip_1_out_16), .out_17(videochip_1_out_17),
    .out_18(videochip_1_out_18), .out_19(videochip_1_out_19), .out_20(videochip_1_out_20),
    .EN(controlunit_1_en_2), .EN_2(videochip_1_en_2), .ballX(controlunit_1_ballx),
    .ballY_2(videochip_1_bally_2), .ballX_2(videochip_1_ballx_2), .ID_2(videochip_1_id_2),
    .LeftBatY(controlunit_1_leftbaty), .RightBatY(controlunit_1_out_11), .LeftBatY_2(videochip_1_leftbaty_2),
    .RightBatY_2(videochip_1_rightbaty_2));  // open: ID
  VideoChip videochip_2 (
    .ballY(videochip_1_bally_2), .out_13(videochip_2_out_13), .out_14(videochip_2_out_14),
    .out_15(videochip_2_out_15), .out_16(videochip_2_out_16), .out_17(videochip_2_out_17),
    .out_18(videochip_2_out_18), .out_19(videochip_2_out_19), .out_20(videochip_2_out_20),
    .EN(videochip_1_en_2), .EN_2(videochip_2_en_2), .ballX(videochip_1_ballx_2),
    .ballY_2(videochip_2_bally_2), .ballX_2(videochip_2_ballx_2), .ID(videochip_1_id_2),
    .ID_2(videochip_2_id_2), .LeftBatY(videochip_1_leftbaty_2), .RightBatY(videochip_1_rightbaty_2),
    .LeftBatY_2(videochip_2_leftbaty_2), .RightBatY_2(videochip_2_rightbaty_2));
  VideoChip videochip_3 (
    .ballY(videochip_2_bally_2), .out_13(videochip_3_out_13), .out_14(videochip_3_out_14),
    .out_15(videochip_3_out_15), .out_16(videochip_3_out_16), .out_17(videochip_3_out_17),
    .out_18(videochip_3_out_18), .out_19(videochip_3_out_19), .out_20(videochip_3_out_20),
    .EN(videochip_2_en_2), .EN_2(videochip_3_en_2), .ballX(videochip_2_ballx_2),
    .ballY_2(videochip_3_bally_2), .ballX_2(videochip_3_ballx_2), .ID(videochip_2_id_2),
    .ID_2(videochip_3_id_2), .LeftBatY(videochip_2_leftbaty_2), .RightBatY(videochip_2_rightbaty_2),
    .LeftBatY_2(videochip_3_leftbaty_2), .RightBatY_2(videochip_3_rightbaty_2));
  Hex_Digit_Display hex_digit_display_3 (.value(Enemy_Score[3:0]));  // open: dp
  VideoChip videochip_4 (
    .ballY(videochip_3_bally_2), .out_13(videochip_4_out_13), .out_14(videochip_4_out_14),
    .out_15(videochip_4_out_15), .out_16(videochip_4_out_16), .out_17(videochip_4_out_17),
    .out_18(videochip_4_out_18), .out_19(videochip_4_out_19), .out_20(videochip_4_out_20),
    .EN(videochip_3_en_2), .ballX(videochip_3_ballx_2), .ID(videochip_3_id_2),
    .LeftBatY(videochip_3_leftbaty_2), .RightBatY(videochip_3_rightbaty_2));  // open: EN_2, ballY_2, ballX_2, ID_2, LeftBatY_2, RightBatY_2
  Hex_Digit_Display hex_digit_display_4 (.value(Enemy_Score[7:4]));  // open: dp
endmodule

module ControlUnit (
  input  EN,
  input  Clock,
  input  [3:0] Joystick,
  input  [3:0] RightBatY,
  output EN_2,
  output [7:0] My_Score,
  output [7:0] Enemy_Score,
  output [4:0] BallX,
  output [4:0] BallY,
  output [4:0] LeftBatY,
  output [4:0] out_11
);

  wire and_1_out, and_2_out, and_3_out, and_4_out, and_5_out, and_6_out, and_7_out, and_8_out, buffer_1_out,
       comparator_1_eq, comparator_3_eq, comparator_4_eq, comparator_5_eq, comparator_6_eq, comparator_7_eq,
       comparator_8_eq, comparator_9_gt, comparator_10_eq, comparator_11_gt, comparator_12_eq, d_ff_1_q,
       d_ff_1_qn, d_ff_2_q, d_ff_2_qn, not_1_out, or_1_out, or_2_out, or_3_out, or_6_out,
       pull_resistor_3_node, X_q, X_qn, Y_q, Y_qn;
  wire [0:0] pull_resistor_6_node, pull_resistor_8_node;
  wire [2:0] priority_encoder_1_out;
  wire [4:0] adder_1_out, adder_2_out, adder_3_out, multiplexer_1_out, multiplexer_2_out, multiplexer_3_out,
       subtractor_1_out, subtractor_2_out, subtractor_3_out;
  wire [5:0] bitadder_1_out, bitadder_2_out, bitadder_3_out, bitadder_4_out;
  wire [7:0] counter_1_q, counter_2_q;
  wire [7:4] divider_1_out, divider_1_rem, divider_2_out, divider_2_rem;
  wire [31:0] decoder_1_out0, decoder_2_out0, decoder_3_out0, decoder_4_out0, or_4_out, or_5_out, xor_1_out,
       xor_2_out;
  wire [31:31] pull_resistor_5_node, pull_resistor_7_node;

  not not_1 (not_1_out, EN);
  Adder #(.width(5)) adder_1 (.a(LeftBatY), .b(5'b00001), .out(adder_1_out));  // open: cin, cout
  Subtractor #(.width(5)) subtractor_1 (.a(LeftBatY), .b(5'b00001), .out(subtractor_1_out));  // open: bin, bout
  Priority_Encoder #(.disabled(0)) priority_encoder_1 (
    .in1(and_1_out), .in2(and_2_out), .in3(comparator_1_eq), .in4(pull_resistor_3_node),
    .out(priority_encoder_1_out));  // open: in0, in5, in6, in7, en_in, gs, en_out
  or or_1 (or_1_out, not_1_out, or_6_out);
  Multiplexer #(.select(3), .width(5), .enable("false")) multiplexer_1 (
    .in0(LeftBatY), .in1(adder_1_out), .in2(subtractor_1_out), .in3(5'b11101), .in4(5'b00001),
    .out(multiplexer_1_out), .sel(priority_encoder_1_out));  // open: in5, in6, in7
  Pull_Resistor pull_resistor_1 (.node(priority_encoder_1_out));
  and and_1 (and_1_out, ~Joystick[3], ~Joystick[2], ~Joystick[1], Joystick[0]);  // AND_Gate
  Subtractor #(.width(5)) subtractor_2 (.a(BallX), .b(5'b00001), .out(subtractor_2_out));  // open: bin, bout
  Adder #(.width(5)) adder_2 (.a(BallX), .b(5'b00001), .out(adder_2_out));  // open: cin, cout
  D_Flip_Flop d_ff_1 (.clk(Clock), .D(d_ff_1_qn), .Q(d_ff_1_q), .Qn(d_ff_1_qn));  // open: preset, en, reset
  D_Flip_Flop d_ff_2 (.clk(d_ff_1_q), .D(d_ff_2_qn), .Q(d_ff_2_q), .Qn(d_ff_2_qn));  // open: preset, en, reset
  Subtractor #(.width(5)) subtractor_3 (.a(BallY), .b(5'b00001), .out(subtractor_3_out));  // open: bin, bout
  Adder #(.width(5)) adder_3 (.a(BallY), .b(5'b00001), .out(adder_3_out));  // open: cin, cout
  Register #(.width(5)) register_1 (.D(multiplexer_1_out), .Q(LeftBatY), .clk(Clock), .clr(or_1_out));  // open: en
  and and_2 (and_2_out, Joystick[0], Joystick[1], Joystick[2], Joystick[3]);
  buf buffer_1 (buffer_1_out, and_3_out);
  D_Flip_Flop X (.clk(or_2_out), .D(X_qn), .Q(X_q), .Qn(X_qn), .preset(or_1_out));  // open: en, reset
  Comparator #(.width(5), .mode("unsigned")) comparator_1 (
    .a(adder_1_out), .b({5{1'b0}}), .eq(comparator_1_eq));  // open: gt, lt
  Pull_Resistor pull_resistor_2 (.node(comparator_1_eq));
  Pull_Resistor pull_resistor_3 (.node(pull_resistor_3_node));
  Comparator #(.width(5), .mode("unsigned")) comparator_2 (
    .a(subtractor_1_out), .b({5{1'b1}}), .eq(pull_resistor_3_node));  // open: gt, lt
  Counter #(.width(5), .max('h1f)) BatY (
    .load(and_3_out), .Q(out_11), .clk(buffer_1_out), .clr(or_1_out));  // open: D, count, carry
  Pull_Resistor pull_resistor_4 (.node(buffer_1_out));
  buf buffer_2 (buffer_1_out, and_4_out);
  and and_3 (and_3_out, RightBatY[0], RightBatY[1], RightBatY[2], RightBatY[3], Clock);
  and and_4 (and_4_out, ~RightBatY[3], ~RightBatY[2], ~RightBatY[1], RightBatY[0], Clock);  // AND_Gate
  D_Flip_Flop Y (.clk(or_3_out), .D(Y_qn), .Q(Y_q), .Qn(Y_qn), .preset(or_1_out));  // open: en, reset
  Register #(.width(5)) u_ballX (.D(multiplexer_2_out), .Q(BallX), .clk(d_ff_2_q), .clr(or_1_out));  // open: en
  Multiplexer #(.width(5), .enable("false")) multiplexer_2 (
    .in0(subtractor_2_out), .in1(adder_2_out), .out(multiplexer_2_out), .sel(X_q));
  Multiplexer #(.width(5), .enable("false")) multiplexer_3 (
    .in0(subtractor_3_out), .in1(adder_3_out), .out(multiplexer_3_out), .sel(Y_q));
  Register #(.width(5)) u_ballY (.D(multiplexer_3_out), .Q(BallY), .clk(d_ff_2_q), .clr(or_1_out));  // open: en
  Decoder #(.select(5), .disabled(0), .enable("false")) decoder_1 (
    .out0(decoder_1_out0[0]), .out1(decoder_1_out0[1]), .out2(decoder_1_out0[2]), .out3(decoder_1_out0[3]),
    .out4(decoder_1_out0[4]), .out5(decoder_1_out0[5]), .out6(decoder_1_out0[6]), .out7(decoder_1_out0[7]),
    .out8(decoder_1_out0[8]), .out9(decoder_1_out0[9]), .out10(decoder_1_out0[10]),
    .out11(decoder_1_out0[11]), .out12(decoder_1_out0[12]), .out13(decoder_1_out0[13]),
    .out14(decoder_1_out0[14]), .out15(decoder_1_out0[15]), .out16(decoder_1_out0[16]),
    .out17(decoder_1_out0[17]), .out18(decoder_1_out0[18]), .out19(decoder_1_out0[19]),
    .out20(decoder_1_out0[20]), .out21(decoder_1_out0[21]), .out22(decoder_1_out0[22]),
    .out23(decoder_1_out0[23]), .out24(decoder_1_out0[24]), .out25(decoder_1_out0[25]),
    .out26(decoder_1_out0[26]), .out27(decoder_1_out0[27]), .out28(decoder_1_out0[28]),
    .out29(decoder_1_out0[29]), .out30(decoder_1_out0[30]), .out31(decoder_1_out0[31]), .sel(LeftBatY));
  Comparator #(.width(5), .mode("unsigned")) comparator_3 (
    .a({5{1'b1}}), .b(BallY), .eq(comparator_3_eq));  // open: gt, lt
  Comparator #(.width(5), .mode("unsigned")) comparator_4 (
    .a({5{1'b0}}), .b(BallY), .eq(comparator_4_eq));  // open: gt, lt
  Pull_Resistor pull_resistor_5 (.node(pull_resistor_5_node[31]));
  Pull_Resistor pull_resistor_6 (.node(pull_resistor_6_node[0]));
  Comparator #(.width(5), .mode("unsigned")) comparator_5 (
    .a({5{1'b1}}), .b(BallX), .eq(comparator_5_eq));  // open: gt, lt
  or or_2 (or_2_out, comparator_5_eq, comparator_6_eq, and_7_out, and_8_out);
  Comparator #(.width(5), .mode("unsigned")) comparator_6 (
    .a({5{1'b0}}), .b(BallX), .eq(comparator_6_eq));  // open: gt, lt
  or or_3 (or_3_out, comparator_3_eq, comparator_4_eq);
  Decoder #(.select(5), .disabled(0), .enable("false")) decoder_2 (
    .out0(decoder_2_out0[0]), .out1(decoder_2_out0[1]), .out2(decoder_2_out0[2]), .out3(decoder_2_out0[3]),
    .out4(decoder_2_out0[4]), .out5(decoder_2_out0[5]), .out6(decoder_2_out0[6]), .out7(decoder_2_out0[7]),
    .out8(decoder_2_out0[8]), .out9(decoder_2_out0[9]), .out10(decoder_2_out0[10]),
    .out11(decoder_2_out0[11]), .out12(decoder_2_out0[12]), .out13(decoder_2_out0[13]),
    .out14(decoder_2_out0[14]), .out15(decoder_2_out0[15]), .out16(decoder_2_out0[16]),
    .out17(decoder_2_out0[17]), .out18(decoder_2_out0[18]), .out19(decoder_2_out0[19]),
    .out20(decoder_2_out0[20]), .out21(decoder_2_out0[21]), .out22(decoder_2_out0[22]),
    .out23(decoder_2_out0[23]), .out24(decoder_2_out0[24]), .out25(decoder_2_out0[25]),
    .out26(decoder_2_out0[26]), .out27(decoder_2_out0[27]), .out28(decoder_2_out0[28]),
    .out29(decoder_2_out0[29]), .out30(decoder_2_out0[30]), .out31(decoder_2_out0[31]),
    .sel(multiplexer_3_out));
  assign or_4_out = {pull_resistor_5_node[31], decoder_1_out0[31:1]} | decoder_1_out0 | {decoder_1_out0[30:0], pull_resistor_6_node[0]};  // OR_Gate or_4, 32 bits wide
  Decoder #(.select(5), .disabled(0), .enable("false")) decoder_3 (
    .out0(decoder_3_out0[0]), .out1(decoder_3_out0[1]), .out2(decoder_3_out0[2]), .out3(decoder_3_out0[3]),
    .out4(decoder_3_out0[4]), .out5(decoder_3_out0[5]), .out6(decoder_3_out0[6]), .out7(decoder_3_out0[7]),
    .out8(decoder_3_out0[8]), .out9(decoder_3_out0[9]), .out10(decoder_3_out0[10]),
    .out11(decoder_3_out0[11]), .out12(decoder_3_out0[12]), .out13(decoder_3_out0[13]),
    .out14(decoder_3_out0[14]), .out15(decoder_3_out0[15]), .out16(decoder_3_out0[16]),
    .out17(decoder_3_out0[17]), .out18(decoder_3_out0[18]), .out19(decoder_3_out0[19]),
    .out20(decoder_3_out0[20]), .out21(decoder_3_out0[21]), .out22(decoder_3_out0[22]),
    .out23(decoder_3_out0[23]), .out24(decoder_3_out0[24]), .out25(decoder_3_out0[25]),
    .out26(decoder_3_out0[26]), .out27(decoder_3_out0[27]), .out28(decoder_3_out0[28]),
    .out29(decoder_3_out0[29]), .out30(decoder_3_out0[30]), .out31(decoder_3_out0[31]), .sel(out_11));
  Decoder #(.select(5), .disabled(0), .enable("false")) decoder_4 (
    .out0(decoder_4_out0[0]), .out1(decoder_4_out0[1]), .out2(decoder_4_out0[2]), .out3(decoder_4_out0[3]),
    .out4(decoder_4_out0[4]), .out5(decoder_4_out0[5]), .out6(decoder_4_out0[6]), .out7(decoder_4_out0[7]),
    .out8(decoder_4_out0[8]), .out9(decoder_4_out0[9]), .out10(decoder_4_out0[10]),
    .out11(decoder_4_out0[11]), .out12(decoder_4_out0[12]), .out13(decoder_4_out0[13]),
    .out14(decoder_4_out0[14]), .out15(decoder_4_out0[15]), .out16(decoder_4_out0[16]),
    .out17(decoder_4_out0[17]), .out18(decoder_4_out0[18]), .out19(decoder_4_out0[19]),
    .out20(decoder_4_out0[20]), .out21(decoder_4_out0[21]), .out22(decoder_4_out0[22]),
    .out23(decoder_4_out0[23]), .out24(decoder_4_out0[24]), .out25(decoder_4_out0[25]),
    .out26(decoder_4_out0[26]), .out27(decoder_4_out0[27]), .out28(decoder_4_out0[28]),
    .out29(decoder_4_out0[29]), .out30(decoder_4_out0[30]), .out31(decoder_4_out0[31]),
    .sel(multiplexer_2_out));
  Pull_Resistor pull_resistor_7 (.node(pull_resistor_7_node[31]));
  Pull_Resistor pull_resistor_8 (.node(pull_resistor_8_node[0]));
  assign xor_1_out = or_4_out ^ decoder_2_out0;  // XOR_Gate xor_1, 32 bits wide
  // Probe on decoder_4_out0
  assign or_5_out = {pull_resistor_7_node[31], decoder_3_out0[31:1]} | decoder_3_out0 | {decoder_3_out0[30:0], pull_resistor_8_node[0]};  // OR_Gate or_5, 32 bits wide
  Comparator #(.width(5), .mode("unsigned")) comparator_7 (
    .a({5{1'b0}}), .b(BallX), .eq(comparator_7_eq));  // open: gt, lt
  Comparator #(.width(5), .mode("unsigned")) comparator_8 (
    .a({5{1'b1}}), .b(multiplexer_2_out), .eq(comparator_8_eq));  // open: gt, lt
  BitAdder #(.width(32)) bitadder_1 (.in0(or_4_out), .out(bitadder_1_out));
  BitAdder #(.width(32)) bitadder_2 (.in0(xor_1_out), .out(bitadder_2_out));
  assign xor_2_out = or_5_out ^ decoder_2_out0;  // XOR_Gate xor_2, 32 bits wide
  or or_6 (or_6_out, and_5_out, and_6_out);
  and and_5 (and_5_out, ~X_q, comparator_7_eq);  // AND_Gate
  and and_6 (and_6_out, X_q, comparator_8_eq);
  Comparator #(.width(6), .mode("unsigned")) comparator_9 (
    .a(bitadder_1_out), .b(bitadder_2_out), .gt(comparator_9_gt));  // open: eq, lt
  and and_7 (and_7_out, comparator_9_gt, comparator_10_eq);
  Comparator #(.width(32), .mode("unsigned")) comparator_10 (
    .a(decoder_4_out0), .b(32'h8), .eq(comparator_10_eq));  // open: gt, lt
  BitAdder #(.width(32)) bitadder_3 (.in0(or_5_out), .out(bitadder_3_out));
  Comparator #(.width(6), .mode("unsigned")) comparator_11 (
    .a(bitadder_3_out), .b(bitadder_4_out), .gt(comparator_11_gt));  // open: eq, lt
  BitAdder #(.width(32)) bitadder_4 (.in0(xor_2_out), .out(bitadder_4_out));
  Comparator #(.width(32), .mode("unsigned")) comparator_12 (
    .a(decoder_4_out0), .b(32'h10000000), .eq(comparator_12_eq));  // open: gt, lt
  and and_8 (and_8_out, comparator_11_gt, comparator_12_eq);
  Counter #(.max('h63)) counter_1 (.Q(counter_1_q), .clk(and_5_out));  // open: load, D, count, carry, clr
  Counter counter_2 (.Q(counter_2_q), .clk(and_6_out));  // open: load, D, count, carry, clr
  Divider divider_1 (
    .a(counter_1_q), .b(8'ha), .out({divider_1_out, Enemy_Score[3:0]}),
    .rem({divider_1_rem, Enemy_Score[7:4]}));  // open: upper
  Divider divider_2 (
    .a(counter_2_q), .b(8'ha), .out({divider_2_out, My_Score[3:0]}), .rem({divider_2_rem, My_Score[7:4]}));  // open: upper

  assign EN_2 = EN;

  // Notes on the sheet:
  //   buffer_1 drives only 1 and floats otherwise
  //   buffer_2 drives only 1 and floats otherwise
endmodule

module VideoChip (
  input  EN,
  input  [4:0] ballY,
  input  [4:0] ballX,
  input  [1:0] ID,
  input  [4:0] LeftBatY,
  input  [4:0] RightBatY,
  output EN_2,
  output [4:0] ballY_2,
  output [4:0] ballX_2,
  output [1:0] ID_2,
  output [4:0] LeftBatY_2,
  output [4:0] RightBatY_2,
  output [31:0] out_13,
  output [31:0] out_14,
  output [31:0] out_15,
  output [31:0] out_16,
  output [31:0] out_17,
  output [31:0] out_18,
  output [31:0] out_19,
  output [31:0] out_20
);

  wire comparator_1_eq;
  wire [31:0] demultiplexer_1_out0, demultiplexer_2_out3, demultiplexer_2_out4, leftbatconstructor_1_out_4,
       rightbatconstructor_1_out_4;

  Pull_Resistor pull_resistor_1 (.node(EN));
  Pull_Resistor pull_resistor_2 (.node(ballY));
  Pull_Resistor pull_resistor_3 (.node(ballX));
  Pull_Resistor pull_resistor_4 (.node(ID));
  Pull_Resistor pull_resistor_5 (.node(LeftBatY));
  Pull_Resistor pull_resistor_6 (.node(RightBatY));
  LeftBatConstructor leftbatconstructor_1 (.EN(EN), .in_2(LeftBatY), .in_3(ID), .out_4(leftbatconstructor_1_out_4));
  RightBatConstructor rightbatconstructor_1 (
    .in_1(EN), .in_2(RightBatY), .in_3(ID), .out_4(rightbatconstructor_1_out_4));
  Demultiplexer #(.select(5)) demultiplexer_1 (
    .out0(demultiplexer_1_out0[0]), .out1(demultiplexer_1_out0[1]), .out2(demultiplexer_1_out0[2]),
    .out3(demultiplexer_1_out0[3]), .out4(demultiplexer_1_out0[4]), .out5(demultiplexer_1_out0[5]),
    .out6(demultiplexer_1_out0[6]), .out7(demultiplexer_1_out0[7]), .out8(demultiplexer_1_out0[8]),
    .out9(demultiplexer_1_out0[9]), .out10(demultiplexer_1_out0[10]), .out11(demultiplexer_1_out0[11]),
    .out12(demultiplexer_1_out0[12]), .out13(demultiplexer_1_out0[13]), .out14(demultiplexer_1_out0[14]),
    .out15(demultiplexer_1_out0[15]), .out16(demultiplexer_1_out0[16]), .out17(demultiplexer_1_out0[17]),
    .out18(demultiplexer_1_out0[18]), .out19(demultiplexer_1_out0[19]), .out20(demultiplexer_1_out0[20]),
    .out21(demultiplexer_1_out0[21]), .out22(demultiplexer_1_out0[22]), .out23(demultiplexer_1_out0[23]),
    .out24(demultiplexer_1_out0[24]), .out25(demultiplexer_1_out0[25]), .out26(demultiplexer_1_out0[26]),
    .out27(demultiplexer_1_out0[27]), .out28(demultiplexer_1_out0[28]), .out29(demultiplexer_1_out0[29]),
    .out30(demultiplexer_1_out0[30]), .out31(demultiplexer_1_out0[31]), .in(EN), .sel(ballY));  // open: en
  Comparator #(.width(2), .mode("unsigned")) comparator_1 (
    .a(ballX[4:3]), .b(ID), .eq(comparator_1_eq));  // open: gt, lt
  Demultiplexer #(.select(3), .width(32), .disabled(0)) demultiplexer_2 (
    .out0(out_13), .out1(out_14), .out2(out_15), .out3(demultiplexer_2_out3), .out4(demultiplexer_2_out4),
    .out5(out_18), .out6(out_19), .out7(out_20), .in(demultiplexer_1_out0), .sel(ballX[2:0]),
    .en(comparator_1_eq));
  Adder #(.width(2)) adder_1 (.a(ID), .b(2'b01), .out(ID_2));  // open: cin, cout
  assign out_16 = demultiplexer_2_out3 | leftbatconstructor_1_out_4;  // OR_Gate or_1, 32 bits wide
  assign out_17 = demultiplexer_2_out4 | rightbatconstructor_1_out_4;  // OR_Gate or_2, 32 bits wide

  assign ballX_2 = ballX;
  assign ballY_2 = ballY;
  assign EN_2 = EN;
  assign LeftBatY_2 = LeftBatY;
  assign RightBatY_2 = RightBatY;
endmodule

module LeftBatConstructor (
  input  EN,
  input  [4:0] in_2,
  input  [1:0] in_3,
  output [31:0] out_4
);

  wire comparator_1_eq;
  wire [0:0] pull_resistor_3_node;
  wire [31:0] decoder_1_out31, or_1_out;
  wire [31:31] pull_resistor_2_node;

  Pull_Resistor pull_resistor_1 (.node(EN));
  Decoder #(.select(5), .disabled(0)) decoder_1 (
    .out0(decoder_1_out31[0]), .out1(decoder_1_out31[1]), .out2(decoder_1_out31[2]),
    .out3(decoder_1_out31[3]), .out4(decoder_1_out31[4]), .out5(decoder_1_out31[5]),
    .out6(decoder_1_out31[6]), .out7(decoder_1_out31[7]), .out8(decoder_1_out31[8]),
    .out9(decoder_1_out31[9]), .out10(decoder_1_out31[10]), .out11(decoder_1_out31[11]),
    .out12(decoder_1_out31[12]), .out13(decoder_1_out31[13]), .out14(decoder_1_out31[14]),
    .out15(decoder_1_out31[15]), .out16(decoder_1_out31[16]), .out17(decoder_1_out31[17]),
    .out18(decoder_1_out31[18]), .out19(decoder_1_out31[19]), .out20(decoder_1_out31[20]),
    .out21(decoder_1_out31[21]), .out22(decoder_1_out31[22]), .out23(decoder_1_out31[23]),
    .out24(decoder_1_out31[24]), .out25(decoder_1_out31[25]), .out26(decoder_1_out31[26]),
    .out27(decoder_1_out31[27]), .out28(decoder_1_out31[28]), .out29(decoder_1_out31[29]),
    .out30(decoder_1_out31[30]), .out31(decoder_1_out31[31]), .sel(in_2), .en(EN));
  Pull_Resistor pull_resistor_2 (.node(pull_resistor_2_node[31]));
  Pull_Resistor pull_resistor_3 (.node(pull_resistor_3_node[0]));
  Comparator #(.width(2)) comparator_1 (.a(in_3), .b(2'b00), .eq(comparator_1_eq));  // open: gt, lt
  assign or_1_out = {pull_resistor_2_node[31], decoder_1_out31[31:1]} | decoder_1_out31 | {decoder_1_out31[30:0], pull_resistor_3_node[0]};  // OR_Gate or_1, 32 bits wide
  Pull_Resistor pull_resistor_4 (.node(out_4));
  assign out_4 = comparator_1_eq ? or_1_out : 32'bz;  // Controlled_Buffer controlled_buffer_1
endmodule

module RightBatConstructor (
  input  in_1,
  input  [4:0] in_2,
  input  [1:0] in_3,
  output [31:0] out_4
);

  wire comparator_1_eq;
  wire [0:0] pull_resistor_3_node;
  wire [31:0] decoder_1_out31, or_1_out;
  wire [31:31] pull_resistor_2_node;

  Pull_Resistor pull_resistor_1 (.node(in_1));
  Decoder #(.select(5), .disabled(0)) decoder_1 (
    .out0(decoder_1_out31[0]), .out1(decoder_1_out31[1]), .out2(decoder_1_out31[2]),
    .out3(decoder_1_out31[3]), .out4(decoder_1_out31[4]), .out5(decoder_1_out31[5]),
    .out6(decoder_1_out31[6]), .out7(decoder_1_out31[7]), .out8(decoder_1_out31[8]),
    .out9(decoder_1_out31[9]), .out10(decoder_1_out31[10]), .out11(decoder_1_out31[11]),
    .out12(decoder_1_out31[12]), .out13(decoder_1_out31[13]), .out14(decoder_1_out31[14]),
    .out15(decoder_1_out31[15]), .out16(decoder_1_out31[16]), .out17(decoder_1_out31[17]),
    .out18(decoder_1_out31[18]), .out19(decoder_1_out31[19]), .out20(decoder_1_out31[20]),
    .out21(decoder_1_out31[21]), .out22(decoder_1_out31[22]), .out23(decoder_1_out31[23]),
    .out24(decoder_1_out31[24]), .out25(decoder_1_out31[25]), .out26(decoder_1_out31[26]),
    .out27(decoder_1_out31[27]), .out28(decoder_1_out31[28]), .out29(decoder_1_out31[29]),
    .out30(decoder_1_out31[30]), .out31(decoder_1_out31[31]), .sel(in_2), .en(in_1));
  Pull_Resistor pull_resistor_2 (.node(pull_resistor_2_node[31]));
  Pull_Resistor pull_resistor_3 (.node(pull_resistor_3_node[0]));
  Comparator #(.width(2)) comparator_1 (.a(in_3), .b(2'b11), .eq(comparator_1_eq));  // open: gt, lt
  assign or_1_out = {pull_resistor_2_node[31], decoder_1_out31[31:1]} | decoder_1_out31 | {decoder_1_out31[30:0], pull_resistor_3_node[0]};  // OR_Gate or_1, 32 bits wide
  assign out_4 = comparator_1_eq ? or_1_out : 32'bz;  // Controlled_Buffer controlled_buffer_1
  Pull_Resistor pull_resistor_4 (.node(out_4));
endmodule
